// Digital circuit ALU.dig as structural Verilog
module ALU (
  input  [7:0] inbus,
  input  [1:0] op,
  input  CLk,
  input  Begin,
  input  RST,
  output [7:0] outbus
);

  wire and_5_out, c0, c0_t, c1, c2, c3, c4, c5, c6, c7, c7_5, c8, cL, cnt7, cR, d_ff_1_q, d_ff_2_q, L,
       not_1_out, O_SR, or_4_out, or_7_out, or_9_out, Q__1, shf2_1_o_sl, shf2_1_o_sr, shf2_2_o_sl,
       shf2_2_o_sr, shft;
  wire [0:0] and_1_out;
  wire [1:0] or_3_out, or_6_out;
  wire [3:0] counter_1_out;
  wire [7:0] A, add, and_3_out, and_4_out, driver_1_out, in, M_q, multiplexer_1_out, multiplexer_2_out,
       multiplexer_3_out, O_A, O_Q, Q, xor_1_out;

  or or_1 (shft, cL, cR);
  D_FF d_ff_1 (.D(shft), .C(CLk), .Q(d_ff_1_q));  // open: nQ
  or or_2 (or_3_out[1], d_ff_1_q, c3);
  or or_3 (or_3_out[0], c0_t, c3);
  or or_4 (or_4_out, c0, c0_t, c3, d_ff_1_q);
  // Probe on multiplexer_1_out
  Multiplexer #(.Selector_Bits(2), .Bits(8)) multiplexer_1 (
    .sel(or_3_out), .in_0({8{1'b0}}), .in_1(inbus), .in_2(O_A), .in_3(add), .out(multiplexer_1_out));
  Register #(.Bits(8)) u_A (.D(multiplexer_1_out), .C(CLk), .en(or_4_out), .Q(A));
  // Probe on A
  // Probe on A[6:0]
  // Probe on Q[0]
  or or_5 (or_6_out[0], c1, c5);
  D_FF d_ff_2 (.D(shft), .C(CLk), .Q(d_ff_2_q));  // open: nQ
  and and_1 (and_1_out[0], ~c7_5, ~A[7], c5);  // And
  or or_6 (or_6_out[1], c5, d_ff_2_q);
  // Probe on multiplexer_2_out
  or or_7 (or_7_out, c1, c5, d_ff_2_q);
  and and_2 (L, ~cR, ~cL);  // And
  assign and_3_out = add & {8{c3}};  // And and_3, 8 bits wide
  assign and_4_out = ~{8{c3}} & A;  // And and_4, 8 bits wide
  Multiplexer #(.Selector_Bits(2), .Bits(8)) multiplexer_2 (
    .sel(or_6_out), .in_0({Q[7:1], and_1_out[0]}), .in_1(inbus), .in_2(O_Q), .in_3({Q[7:1], and_1_out[0]}),
    .out(multiplexer_2_out));
  Register #(.Bits(8)) u_Q (.D(multiplexer_2_out), .C(CLk), .en(or_7_out), .Q(Q));
  ALU_CU alu_cu_1 (
    .BGN(Begin), .RST(RST), .CLK(CLk), .CNT7(cnt7), .Q0(Q[0]), .Q_1(Q__1), .A7(A[7]), .OP(op), .c0(c0),
    .c0_2(c0_t), .c1(c1), .c2(c2), .c3(c3), .c4(c4), .cR(cR), .cL(cL), .c5(c5), .c7(c7), .c8(c8), .c6(c6),
    .c7_5(c7_5));
  assign in = and_3_out | and_4_out;  // Or or_8, 8 bits wide
  // Probe on Q[0]
  // Probe on Q
  // Probe on Q[7:1]
  or or_9 (or_9_out, c1, d_ff_2_q);
  Register u_Q__1 (.D(O_SR), .C(CLk), .en(or_9_out), .Q(Q__1));
  // Probe on Q__1
  shf2 shf2_1 (
    .CLK(CLk), .SR(cR), .SL(cL), .IN_SR(A[7]), .IN_SL(shf2_2_o_sl), .IN(in), .LD(L), .O_sr(shf2_1_o_sr),
    .O_sl(shf2_1_o_sl), .O(O_A));
  // Probe on shf2_1_o_sl
  Counter #(.Bits(4)) counter_1 (.en(c6), .C(CLk), .clr(RST), .out(counter_1_out));  // open: ovf
  // Probe on O_A
  not not_1 (not_1_out, A[7]);
  assign driver_1_out = c2 ? inbus : 8'bz;  // Driver driver_1
  // Probe on driver_1_out
  Register #(.Bits(8)) M (.D(driver_1_out), .C(CLk), .en(c2), .Q(M_q));
  assign xor_1_out = {8{c4}} ^ M_q;  // XOr xor_1, 8 bits wide
  shf2 shf2_2 (
    .CLK(CLk), .SR(cR), .SL(cL), .IN_SR(shf2_1_o_sr), .IN_SL(not_1_out), .IN(Q), .LD(L), .O_sr(shf2_2_o_sr),
    .O_sl(shf2_2_o_sl), .O(O_Q));
  // Probe on M_q
  Multiplexer #(.Bits(8)) multiplexer_3 (.sel(and_5_out), .in_0(A), .in_1(O_A), .out(multiplexer_3_out));
  and and_5 (and_5_out, op[0], op[1]);
  and and_6 (cnt7, ~counter_1_out[0], ~counter_1_out[1], ~counter_1_out[2], counter_1_out[3]);  // And
  D_FF d_ff_3 (.D(shf2_2_o_sr), .C(CLk), .Q(O_SR));  // open: nQ
  // Probe on O_Q
  RCA8 Parallel_Adder (.c_in(c4), .Y(xor_1_out), .X(multiplexer_3_out), .Z(add));  // open: c_out
  Multiplexer #(.Selector_Bits(2), .Bits(8)) multiplexer_4 (
    .sel({c8, c7}), .in_0({8{1'b0}}), .in_1(A), .in_2(Q), .in_3({8{1'b0}}), .out(outbus));

  // Other names for the same wires on the sheet: A_7 = A[7]; Q_0 = Q[0]
endmodule
