// Digital circuit ALU_CU.dig as structural Verilog
module ALU_CU (
  input  BGN,
  input  RST,
  input  CLK,
  input  CNT7,
  input  Q0,
  input  Q_1,
  input  A7,
  input  [1:0] OP,
  output c0,
  output c0_2,
  output c1,
  output c2,
  output c3,
  output c4,
  output cR,
  output cL,
  output c5,
  output c7,
  output c8,
  output c6,
  output c7_5
);

  wire adun, and_1_out, and_2_out, and_3_out, and_4_out, and_5_out, and_6_out, and_8_out, and_9_out,
       and_10_out, and_11_out, and_12_out, and_13_out, and_14_out, and_15_out, and_16_out, and_17_out,
       and_19_out, and_24_out, and_30_out, C2_t, C3_t, \end , nand_1_out, not_2_out, not_3_out, not_4_out,
       not_5_out, not_6_out, not_7_out, not_8_out, not_9_out, not_10_out, not_11_out, not_12_out, not_13_out,
       not_14_out, not_15_out, not_16_out, not_17_out, not_18_out, not_19_out, not_20_out, or_1_out,
       or_2_out, or_3_out, or_4_out, or_5_out, or_6_out, or_7_out, or_8_out, rs_ff_1_q, scad,
       \sequncecntmod_1_φ0 , \sequncecntmod_1_φ1 , \sequncecntmod_1_φ2 , \sequncecntmod_1_φ3 ,
       \sequncecntmod_1_φ4 , \sequncecntmod_1_φ5 , xor_1_out;

  or or_1 (or_1_out, \end , RST);
  or or_2 (or_2_out, RST, or_4_out);
  or or_3 (or_3_out, RST, and_2_out);
  nand nand_1 (nand_1_out, \sequncecntmod_1_φ5 , BGN);
  RS_FF rs_ff_1 (.R(or_3_out), .S(and_1_out), .Q(rs_ff_1_q));  // open: nQ
  RS_FF rs_ff_2 (.R(or_2_out), .S(and_2_out), .Q(C2_t));  // open: nQ
  or or_4 (or_4_out, and_4_out, and_3_out);
  RS_FF rs_ff_3 (.R(or_1_out), .S(or_4_out), .Q(C3_t));  // open: nQ
  and and_1 (and_1_out, ~C2_t, ~C3_t, ~\end , nand_1_out);  // And
  and and_2 (and_2_out, \sequncecntmod_1_φ5 , rs_ff_1_q);
  and and_3 (and_3_out, \sequncecntmod_1_φ5 , CNT7);
  and and_4 (and_4_out, or_5_out, \sequncecntmod_1_φ5 );
  or or_5 (or_5_out, scad, adun);
  not not_1 (\end , not_3_out);
  sequnceCNTmod sequncecntmod_1 (
    .CLK(CLK), .BGN(BGN), .RST(RST), .END(\end ), .\Φ0 (\sequncecntmod_1_φ0 ), .\Φ1 (\sequncecntmod_1_φ1 ),
    .\Φ2 (\sequncecntmod_1_φ2 ), .\Φ3 (\sequncecntmod_1_φ3 ), .\Φ4 (\sequncecntmod_1_φ4 ),
    .\Φ5 (\sequncecntmod_1_φ5 ));  // open: Φ6, Φ7
  not not_2 (not_2_out, not_5_out);
  not not_3 (not_3_out, not_2_out);
  not not_4 (not_4_out, not_7_out);
  not not_5 (not_5_out, not_4_out);
  not not_6 (not_6_out, not_9_out);
  not not_7 (not_7_out, not_6_out);
  not not_8 (not_8_out, not_11_out);
  not not_9 (not_9_out, not_8_out);
  and and_5 (and_5_out, ~OP[0], OP[1]);  // And
  xor xor_1 (xor_1_out, Q0, Q_1);
  not not_10 (not_10_out, not_13_out);
  not not_11 (not_11_out, not_10_out);
  and and_6 (and_6_out, OP[0], OP[1]);
  not not_12 (not_12_out, not_15_out);
  not not_13 (not_13_out, not_12_out);
  and and_7 (adun, ~OP[0], ~OP[1]);  // And
  or or_6 (or_6_out, and_6_out, and_5_out);
  and and_8 (and_8_out, and_5_out, xor_1_out, \sequncecntmod_1_φ0 , C2_t);
  and and_9 (and_9_out, C2_t, and_6_out, \sequncecntmod_1_φ3 , A7);
  and and_10 (and_10_out, A7, C3_t, and_6_out, \sequncecntmod_1_φ0 );
  and and_11 (and_11_out, C2_t, \sequncecntmod_1_φ1 , and_6_out);
  and and_12 (and_12_out, c3, and_5_out, Q0, ~Q_1);  // And
  and and_13 (and_13_out, c3, \sequncecntmod_1_φ1 , and_6_out);
  and and_14 (and_14_out, and_5_out, \sequncecntmod_1_φ2 , ~CNT7, C2_t);  // And
  and and_15 (and_15_out, and_6_out, \sequncecntmod_1_φ4 , ~CNT7, C2_t);  // And
  and and_16 (and_16_out, and_5_out, \sequncecntmod_1_φ0 );
  and and_17 (and_17_out, \sequncecntmod_1_φ1 , and_6_out);
  not not_14 (not_14_out, not_17_out);
  not not_15 (not_15_out, not_14_out);
  or or_7 (or_7_out, adun, and_16_out, and_17_out, scad);
  not not_16 (not_16_out, not_19_out);
  not not_17 (not_17_out, not_16_out);
  and and_18 (scad, OP[0], ~OP[1]);  // And
  or or_8 (or_8_out, adun, scad);
  and and_19 (and_19_out, c3, scad);
  not not_18 (not_18_out, not_20_out);
  not not_19 (not_19_out, not_18_out);
  and and_20 (c0, and_5_out, \sequncecntmod_1_φ0 , rs_ff_1_q);
  and and_21 (c0_2, \sequncecntmod_1_φ0 , ~and_5_out, rs_ff_1_q);  // And
  and and_22 (c1, rs_ff_1_q, or_6_out, \sequncecntmod_1_φ1 );
  and and_23 (c2, rs_ff_1_q, \sequncecntmod_1_φ2 );
  and and_24 (and_24_out, or_8_out, \sequncecntmod_1_φ3 );
  or or_9 (c4, and_19_out, and_12_out, and_13_out);
  and and_25 (cR, and_5_out, C2_t, ~CNT7, \sequncecntmod_1_φ1 );  // And
  and and_26 (cL, and_6_out, \sequncecntmod_1_φ0 , C2_t);
  and and_27 (c5, and_6_out, \sequncecntmod_1_φ2 , C2_t);
  or or_10 (c6, and_14_out, and_15_out);
  not not_20 (not_20_out, c8);
  or or_11 (c3, and_24_out, and_8_out, and_9_out, and_10_out, and_11_out);
  and and_28 (c7, C3_t, or_7_out);
  and and_29 (c7_5, and_5_out, \sequncecntmod_1_φ1 , C3_t);
  and and_30 (and_30_out, \sequncecntmod_1_φ2 , C3_t);
  RS_FF rs_ff_4 (.R(RST), .S(and_30_out), .Q(c8));  // open: nQ
  // Probe on CLK

  // Other names for the same wires on the sheet: A_7 = A7; Q_0 = Q0; Q__1 = Q_1
endmodule
