// Digital circuit Dec3to5.dig as structural Verilog
module Dec3to5 (
  input  [2:0] sel,
  output _0,
  output _1,
  output _2,
  output _3,
  output _4,
  output _5
);

  wire not_1_out, not_2_out, not_3_out;

  not not_1 (not_1_out, sel[2]);
  not not_2 (not_2_out, sel[1]);
  not not_3 (not_3_out, sel[0]);
  and and_1 (_0, not_3_out, not_2_out, not_1_out);
  and and_2 (_1, not_1_out, not_2_out, sel[0]);
  and and_3 (_2, not_1_out, sel[1], not_3_out);
  and and_4 (_3, not_1_out, sel[1], sel[0]);
  and and_5 (_4, sel[2], not_2_out, not_3_out);
  and and_6 (_5, sel[2], not_2_out, sel[0]);
  // Pins of 1 and 3 bits meet at sel
endmodule
