// Digital circuit RS_FF_CLK.dig as structural Verilog
module RS_FF_CLK (
  input  S,
  input  R,
  input  CLK,
  output Q,
  output nQ
);

  wire nand_1_out, nand_2_out;

  nand nand_1 (nand_1_out, S, CLK);
  nand nand_2 (nand_2_out, CLK, R);
  nand nand_3 (Q, nand_1_out, nQ);
  nand nand_4 (nQ, Q, nand_2_out);
endmodule
