// Digital circuit SHFT.dig as structural Verilog
module SHFT (
  input  CLK,
  input  DIR,
  input  IN_SR,
  input  IN_SL,
  input  RST,
  input  [7:0] IN,
  input  LD,
  output O_SR,
  output O_SL,
  output [7:0] o
);

  wire and_1_out, and_2_out, and_3_out, and_4_out, and_5_out, and_6_out, and_7_out, and_8_out, and_9_out,
       and_10_out, MX0, MX1, MX2, MX3, MX4, MX5, MX6, MX7, not_1_out, or_1_out, or_2_out, or_3_out, or_4_out,
       or_5_out, or_6_out, or_7_out, or_8_out;

  not not_1 (not_1_out, CLK);
  and and_1 (and_1_out, IN_SR, ~LD);  // And
  Multiplexer multiplexer_1 (.sel(DIR), .in_0(and_1_out), .in_1(o[6]), .out(MX7));
  D_FF d_ff_1 (.D(or_1_out), .CLK(not_1_out), .R(RST), .Q(o[7]));  // open: nQ
  Multiplexer multiplexer_2 (.sel(DIR), .in_0(o[7]), .in_1(o[5]), .out(MX6));
  or or_1 (or_1_out, MX7, and_2_out);
  D_FF d_ff_2 (.D(or_2_out), .CLK(not_1_out), .R(RST), .Q(o[6]));  // open: nQ
  and and_2 (and_2_out, LD, IN[7]);
  or or_2 (or_2_out, MX6, and_3_out);
  and and_3 (and_3_out, LD, IN[6]);
  Multiplexer multiplexer_3 (.sel(DIR), .in_0(o[6]), .in_1(o[4]), .out(MX5));
  and and_4 (and_4_out, LD, IN[5]);
  or or_3 (or_3_out, MX5, and_4_out);
  and and_5 (and_5_out, LD, IN[4]);
  or or_4 (or_4_out, MX4, and_5_out);
  D_FF d_ff_3 (.D(or_3_out), .CLK(not_1_out), .R(RST), .Q(o[5]));  // open: nQ
  and and_6 (and_6_out, LD, IN[3]);
  or or_5 (or_5_out, MX3, and_6_out);
  and and_7 (and_7_out, LD, IN[2]);
  or or_6 (or_6_out, MX2, and_7_out);
  Multiplexer multiplexer_4 (.sel(DIR), .in_0(o[5]), .in_1(o[3]), .out(MX4));
  and and_8 (and_8_out, LD, IN[1]);
  and and_9 (and_9_out, LD, IN[0]);
  or or_7 (or_7_out, MX1, and_8_out);
  D_FF d_ff_4 (.D(or_4_out), .CLK(not_1_out), .R(RST), .Q(o[4]));  // open: nQ
  or or_8 (or_8_out, MX0, and_9_out);
  Multiplexer multiplexer_5 (.sel(DIR), .in_0(o[4]), .in_1(o[2]), .out(MX3));
  D_FF d_ff_5 (.D(or_5_out), .CLK(not_1_out), .R(RST), .Q(o[3]));  // open: nQ
  Multiplexer multiplexer_6 (.sel(DIR), .in_0(o[3]), .in_1(o[1]), .out(MX2));
  D_FF d_ff_6 (.D(or_6_out), .CLK(not_1_out), .R(RST), .Q(o[2]));  // open: nQ
  Multiplexer multiplexer_7 (.sel(DIR), .in_0(o[2]), .in_1(o[0]), .out(MX1));
  D_FF d_ff_7 (.D(or_7_out), .CLK(not_1_out), .R(RST), .Q(o[1]));  // open: nQ
  and and_10 (and_10_out, ~LD, IN_SL);  // And
  Multiplexer multiplexer_8 (.sel(DIR), .in_0(o[1]), .in_1(and_10_out), .out(MX0));
  D_FF d_ff_8 (.D(or_8_out), .CLK(not_1_out), .R(RST), .Q(o[0]));  // open: nQ

  assign O_SL = o[7];
  assign O_SR = o[0];
endmodule
