// Digital circuit cnt7.dig as structural Verilog
module cnt7 (
  input  CLK,
  input  RST,
  output CNT7
);

  wire and_1_out, jk_ff_as_1_nq, jk_ff_as_1_q, jk_ff_as_2_nq, jk_ff_as_2_q, jk_ff_as_3_q;

  JK_FF_AS jk_ff_as_1 (.Set(1'b0), .J(1'b1), .C(CLK), .K(1'b1), .Clr(RST), .Q(jk_ff_as_1_q), .nQ(jk_ff_as_1_nq));
  and and_1 (and_1_out, jk_ff_as_1_q, jk_ff_as_2_q, jk_ff_as_3_q);
  D_FF d_ff_1 (.D(and_1_out), .C(CLK), .Q(CNT7));  // open: nQ
  JK_FF_AS jk_ff_as_2 (
    .Set(1'b0), .J(1'b1), .C(jk_ff_as_1_nq), .K(1'b1), .Clr(RST), .Q(jk_ff_as_2_q), .nQ(jk_ff_as_2_nq));
  JK_FF_AS jk_ff_as_3 (.Set(1'b0), .J(1'b1), .C(jk_ff_as_2_nq), .K(1'b1), .Clr(RST), .Q(jk_ff_as_3_q));  // open: nQ

  // Other names for the same wires on the sheet: RST_N = RST
endmodule
