// Digital circuit Dec3to5.dig as structural Verilog
module Dec3to5 (
  input  [2:0] sel,
  output O0,
  output O1,
  output O2,
  output O3,
  output O4,
  output O5
);

  wire not_1_out, not_2_out, not_3_out;

  not not_1 (not_1_out, sel[2]);
  not not_2 (not_2_out, sel[1]);
  not not_3 (not_3_out, sel[0]);
  and and_1 (O0, not_3_out, not_2_out, not_1_out);
  and and_2 (O1, not_1_out, not_2_out, sel[0]);
  and and_3 (O2, not_1_out, sel[1], not_3_out);
  and and_4 (O3, not_1_out, sel[1], sel[0]);
  and and_5 (O4, sel[2], not_2_out, not_3_out);
  and and_6 (O5, sel[2], not_2_out, sel[0]);
  // Pins of 1 and 3 bits meet at sel
endmodule
