// Digital circuit FAC.dig as structural Verilog
module FAC (
  input  X,
  input  Y,
  input  C_in,
  output Cout,
  output Z
);

  wire and_1_out, and_2_out, and_3_out, xor_1_out;

  or or_1 (Cout, and_3_out, and_2_out, and_1_out);
  and and_1 (and_1_out, Y, C_in);
  and and_2 (and_2_out, X, C_in);
  and and_3 (and_3_out, X, Y);
  xor xor_1 (xor_1_out, X, Y);
  xor xor_2 (Z, xor_1_out, C_in);
endmodule
