// Digital circuit RCA8.dig as structural Verilog
module RCA8 (
  input  c_in,
  input  [7:0] Y,
  input  [7:0] X,
  output c_out,
  output [7:0] Z
);

  wire fac_2_cout, fac_3_cout, fac_4_cout, fac_5_cout, fac_6_cout, fac_7_cout, fac_8_cout;

  FAC fac_1 (.X(X[7]), .Y(Y[7]), .C_in(fac_2_cout), .Cout(c_out), .Z(Z[7]));
  FAC fac_2 (.X(X[6]), .Y(Y[6]), .C_in(fac_3_cout), .Cout(fac_2_cout), .Z(Z[6]));
  FAC fac_3 (.X(X[5]), .Y(Y[5]), .C_in(fac_4_cout), .Cout(fac_3_cout), .Z(Z[5]));
  FAC fac_4 (.X(X[4]), .Y(Y[4]), .C_in(fac_5_cout), .Cout(fac_4_cout), .Z(Z[4]));
  FAC fac_5 (.X(X[3]), .Y(Y[3]), .C_in(fac_6_cout), .Cout(fac_5_cout), .Z(Z[3]));
  FAC fac_6 (.X(X[2]), .Y(Y[2]), .C_in(fac_7_cout), .Cout(fac_6_cout), .Z(Z[2]));
  FAC fac_7 (.X(X[1]), .Y(Y[1]), .C_in(fac_8_cout), .Cout(fac_7_cout), .Z(Z[1]));
  FAC fac_8 (.X(X[0]), .Y(Y[0]), .C_in(c_in), .Cout(fac_8_cout), .Z(Z[0]));
endmodule
