// Digital circuit sequnceCNTmod.dig as structural Verilog
module sequnceCNTmod (
  input  CLK,
  input  BGN,
  input  RST,
  input  END,
  output \Φ0 ,
  output \Φ1 ,
  output \Φ2 ,
  output \Φ3 ,
  output \Φ4 ,
  output \Φ5 
);

  wire and_1_out, counter3_1_p4, rs_ff_1_q;

  RS_FF rs_ff_1 (.R(END), .S(BGN), .Q(rs_ff_1_q));  // open: nQ
  and and_1 (and_1_out, rs_ff_1_q, RST);
  // counter3 counter3_1: pin names not known; wires that end beside it: rs_ff_1_q, CLK, and_1_out, counter3_1_p4
  // Dec3to5 dec3to5_1: pin names not known; wires that end beside it: \Φ5 , \Φ4 , \Φ3 , \Φ2 , \Φ1 , counter3_1_p4, \Φ0 
endmodule
