// Digital circuit testshft.dig as structural Verilog
module testshft (
  input  CLK,
  input  RST,
  input  LD,
  output o_sr,
  output [7:0] o1,
  output [7:0] o2,
  output out_7
);

  wire osl, shft_1_o_sr;

  SHFT shft_1 (
    .CLK(CLK), .DIR(1'b1), .IN_SR(1'b1), .IN_SL(osl), .RST(RST), .IN(8'h47), .LD(LD), .O_SR(shft_1_o_sr),
    .O_SL(out_7), .o(o1));
  SHFT shft_2 (
    .CLK(CLK), .DIR(1'b1), .IN_SR(shft_1_o_sr), .IN_SL(1'b1), .RST(RST), .IN(8'h23), .LD(LD), .O_SR(o_sr),
    .O_SL(osl), .o(o2));
endmodule
