// Digital circuit sequnceCNTmod.dig as structural Verilog
module sequnceCNTmod (
  input  CLK,
  input  BGN,
  input  RST,
  input  END,
  output \Φ0 ,
  output \Φ1 ,
  output \Φ2 ,
  output \Φ3 ,
  output \Φ4 ,
  output \Φ5 ,
  output \Φ6 ,
  output \Φ7 
);

  wire and_1_out, rs_ff_as_1_q;
  wire [2:0] counter3_1_out;

  RS_FF_AS rs_ff_as_1 (.S(BGN), .R(END), .Q(rs_ff_as_1_q));  // open: nQ
  and and_1 (and_1_out, rs_ff_as_1_q, RST);
  counter3 counter3_1 (.CNT(rs_ff_as_1_q), .CLK(CLK), .RST(and_1_out), .OUT(counter3_1_out));
  Decoder #(.Selector_Bits(3)) decoder_1 (
    .sel(counter3_1_out), .out_0(\Φ0 ), .out_1(\Φ1 ), .out_2(\Φ2 ), .out_3(\Φ3 ), .out_4(\Φ4 ), .out_5(\Φ5 ),
    .out_6(\Φ6 ), .out_7(\Φ7 ));
endmodule
