// Digital circuit shf2.dig as structural Verilog
module shf2 (
  input  CLK,
  input  SR,
  input  SL,
  input  IN_SR,
  input  IN_SL,
  input  [7:0] IN,
  input  LD,
  output O_sr,
  output O_sl,
  output [7:0] O
);

  wire and_1_out, and_2_out, and_3_out, and_4_out, and_5_out, and_6_out, and_7_out, and_8_out, and_9_out,
       and_10_out, and_11_out, and_12_out, and_13_out, and_14_out, and_15_out, and_16_out, and_17_out,
       and_18_out, and_19_out, and_20_out, and_21_out, and_22_out, and_23_out, and_24_out, or_1_out,
       or_2_out, or_3_out, or_4_out, or_5_out, or_6_out, or_7_out, or_8_out;

  and and_1 (and_1_out, IN_SR, SR);
  and and_2 (and_2_out, SL, O[6]);
  and and_3 (and_3_out, IN[7], LD);
  or or_1 (or_1_out, and_1_out, and_3_out, and_2_out);
  RS_FF rs_ff_1 (.S(or_1_out), .C(CLK), .R(~or_1_out), .Q(O[7]));  // open: nQ
  and and_4 (and_4_out, O[7], SR);
  and and_5 (and_5_out, SL, O[5]);
  and and_6 (and_6_out, IN[6], LD);
  or or_2 (or_2_out, and_4_out, and_6_out, and_5_out);
  RS_FF rs_ff_2 (.S(or_2_out), .C(CLK), .R(~or_2_out), .Q(O[6]));  // open: nQ
  and and_7 (and_7_out, O[6], SR);
  and and_8 (and_8_out, SL, O[4]);
  and and_9 (and_9_out, IN[5], LD);
  or or_3 (or_3_out, and_7_out, and_9_out, and_8_out);
  RS_FF rs_ff_3 (.S(or_3_out), .C(CLK), .R(~or_3_out), .Q(O[5]));  // open: nQ
  and and_10 (and_10_out, O[5], SR);
  and and_11 (and_11_out, SL, O[3]);
  and and_12 (and_12_out, IN[4], LD);
  or or_4 (or_4_out, and_10_out, and_12_out, and_11_out);
  RS_FF rs_ff_4 (.S(or_4_out), .C(CLK), .R(~or_4_out), .Q(O[4]));  // open: nQ
  and and_13 (and_13_out, O[4], SR);
  and and_14 (and_14_out, SL, O[2]);
  and and_15 (and_15_out, IN[3], LD);
  or or_5 (or_5_out, and_13_out, and_15_out, and_14_out);
  RS_FF rs_ff_5 (.S(or_5_out), .C(CLK), .R(~or_5_out), .Q(O[3]));  // open: nQ
  and and_16 (and_16_out, O[3], SR);
  and and_17 (and_17_out, SL, O[1]);
  and and_18 (and_18_out, IN[2], LD);
  or or_6 (or_6_out, and_16_out, and_18_out, and_17_out);
  RS_FF rs_ff_6 (.S(or_6_out), .C(CLK), .R(~or_6_out), .Q(O[2]));  // open: nQ
  and and_19 (and_19_out, O[2], SR);
  and and_20 (and_20_out, SL, O[0]);
  and and_21 (and_21_out, IN[1], LD);
  or or_7 (or_7_out, and_19_out, and_21_out, and_20_out);
  RS_FF rs_ff_7 (.S(or_7_out), .C(CLK), .R(~or_7_out), .Q(O[1]));  // open: nQ
  and and_22 (and_22_out, O[1], SR);
  and and_23 (and_23_out, SL, IN_SL);
  and and_24 (and_24_out, IN[0], LD);
  or or_8 (or_8_out, and_22_out, and_24_out, and_23_out);
  RS_FF rs_ff_8 (.S(or_8_out), .C(CLK), .R(~or_8_out), .Q(O[0]));  // open: nQ

  assign O_sl = O[7];
  assign O_sr = O[0];

  // Other names for the same wires on the sheet: _0 = IN[0]; _1 = IN[1]; _2 = IN[2]; _3 = IN[3]; _4 = IN[4];
  //   _5 = IN[5]; _6 = IN[6]; _7 = IN[7]
endmodule
